# Fritzing sketch SC² prototype circuit diagram (saved by Fritzing 0.9.3b)
breadboards: 1

parts:
  U1 = NodeMCU V3.0
  Bauteil1 = TMP006 Thermopile Sensor
  LED1 = RGB LED (com. cathode, rgb) [package="5 mm [THT]"]
  R1 = Resistor [tolerance=±5% resistance=100 package=THT]
  R2 = Resistor [tolerance=±5% resistance=100 package=THT]
  R3 = Resistor [tolerance=±5% resistance=100 package=THT]

nets:
  N1: U1.D1, Bauteil1.SCL
  N2: U1.D2, Bauteil1.SDA
  3V3: U1.3V3, Bauteil1.VCC
  GND: U1.GND, Bauteil1.GND, LED1.common_cathode
  N3: U1.D5, R3.Pin_1
  N4: U1.D6, R2.Pin_1
  N5: U1.D7, R1.Pin_1
  N6: LED1.red_anode, R3.Pin_0
  N7: LED1.green_anode, R2.Pin_0
  N8: LED1.blue_anode, R1.Pin_0

custom parts:
  NodeMCU V3.0: ESP8266 based NodeMCU
  TMP006 Thermopile Sensor: Unlike all the other temperature sensors we have, this breakout has a really cool IR sensor from TI that can measure the temperature of an object without touching it! Simply point the sensor towards what you want to measure and it will detect the temperature by absorbing IR waves emitted. The embedded thermopile sensor generates a very very small voltage depending on how much IR there is, and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
